# Fritzing sketch Untitled Sketch (saved by Fritzing 0.9.3b)
breadboards: 1

parts:
  Part1 = Arduino Uno (Rev3) - ICSP
  LCD1 = LCD screen
  LCM1602_IIC1 = LCM1602 IIC [part_number="LCM1602 IIC" chip_label="LCM1602 IIC" package="DIP (Dual Inline) [THT]"]
  JP1 = Jumper [package=sj_2s]
  U1 = TCRT5000 [package=THT]
  R1 = Resistor [tolerance=±5% resistance=220 package="2010 [SMD]"]
  R2 = Resistor [tolerance=±5% resistance=220 package="2010 [SMD]"]
  U2 = TCRT5000 [package=THT]
  R3 = Resistor [tolerance=±5% resistance=220 package="2010 [SMD]"]
  R4 = Resistor [tolerance=±5% resistance=220 package="2010 [SMD]"]
  U3 = TCRT5000 [package=THT]
  R5 = Resistor [tolerance=±5% resistance=220 package="2010 [SMD]"]
  R6 = Resistor [tolerance=±5% resistance=220 package="2010 [SMD]"]
  R7 = Resistor [tolerance=±5% resistance=220 package="2010 [SMD]"]
  R8 = Resistor [tolerance=±5% resistance=220 package="2010 [SMD]"]
  U4 = TCRT5000 [package=THT]
  U5 = TCRT5000 [package=THT]
  U6 = TCRT5000 [package=THT]
  U7 = TCRT5000 [package=THT]
  U8 = TCRT5000 [package=THT]
  R9 = Resistor [tolerance=±5% resistance=220 package="2010 [SMD]"]
  R10 = Resistor [tolerance=±5% resistance=220 package="2010 [SMD]"]
  R11 = Resistor [tolerance=±5% resistance=220 package="2010 [SMD]"]
  R12 = Resistor [tolerance=±5% resistance=220 package="2010 [SMD]"]
  R13 = Resistor [tolerance=±5% resistance=220 package="2010 [SMD]"]
  R14 = Resistor [tolerance=±5% resistance=220 package="2010 [SMD]"]
  R15 = Resistor [tolerance=±5% resistance=220 package="2010 [SMD]"]
  R16 = Resistor [tolerance=±5% resistance=220 package="2010 [SMD]"]
  J2 = Basic Servo

nets:
  N1: Part1.A0, U1.Pin_1, U1.Pin_2, R2.Pin_0
  N2: Part1.A1, U2.Pin_1, U2.Pin_2, R4.Pin_0
  N3: Part1.A2, U3.Pin_1, U3.Pin_2, R6.Pin_0
  N4: Part1.A3, R8.Pin_0, U4.Pin_1, U4.Pin_2
  N5: Part1.A4/SDA, LCM1602_IIC1.SDA
  N6: Part1.A5/SCL, LCM1602_IIC1.SCL
  GND: Part1.D10_PWM/SS, Part1.GND, LCM1602_IIC1.GND, U8.Pin_1, U8.Pin_2, R16.Pin_0
  N7: Part1.D11_PWM/MOSI, U7.Pin_1, U7.Pin_2, R14.Pin_0
  N8: Part1.D12/MISO, U6.Pin_1, U6.Pin_2, R12.Pin_0
  N9: Part1.D13/SCK, U5.Pin_1, U5.Pin_2, R10.Pin_0
  N10: Part1.D7, J2.pulse
  5V: Part1.5V, LCM1602_IIC1.VCC, R1.Pin_1, R2.Pin_1, R3.Pin_1, R4.Pin_1, R5.Pin_1, R6.Pin_1, R7.Pin_1, R8.Pin_1, R9.Pin_1, R10.Pin_1, R11.Pin_1, R12.Pin_1, R13.Pin_1, R14.Pin_1, R15.Pin_1, R16.Pin_1
  VSS: LCD1.VSS, LCM1602_IIC1.VSS
  VDD: LCD1.VDD, LCM1602_IIC1.VDD
  N11: LCD1.V0, LCM1602_IIC1.V0
  N12: LCD1.RS, LCM1602_IIC1.RS
  N13: LCD1.R/W, LCM1602_IIC1.RW
  N14: LCD1.E, LCM1602_IIC1.E
  N15: LCD1.DB0, LCM1602_IIC1.D0
  N16: LCD1.DB1, LCM1602_IIC1.D1
  N17: LCD1.DB2, LCM1602_IIC1.D2
  N18: LCD1.DB3, LCM1602_IIC1.D3
  N19: LCD1.DB4, LCM1602_IIC1.D4
  N20: LCD1.DB5, LCM1602_IIC1.D5
  N21: LCD1.DB6, LCM1602_IIC1.D6
  N22: LCD1.DB7, LCM1602_IIC1.D7
  N23: LCD1.LED+, LCM1602_IIC1.A
  N24: LCD1.LED-, LCM1602_IIC1.K
  N25: LCM1602_IIC1.LED_A, JP1.1
  N26: LCM1602_IIC1.LED_B, JP1.2
  N27: U1.Pin_3, U1.Pin_4, R1.Pin_0
  N28: U2.Pin_3, U2.Pin_4, R3.Pin_0
  N29: U3.Pin_3, U3.Pin_4, R5.Pin_0
  N30: R7.Pin_0, U4.Pin_3, U4.Pin_4
  N31: U5.Pin_3, U5.Pin_4, R9.Pin_0
  N32: U6.Pin_3, U6.Pin_4, R11.Pin_0
  N33: U7.Pin_3, U7.Pin_4, R13.Pin_0
  N34: U8.Pin_3, U8.Pin_4, R15.Pin_0

custom parts:
  LCM1602 IIC: I2C-Module to use a 1602 or 2004 LCD on with the wire.h libory Serial LCD Modul
  TCRT5000: TCRT5000 optical reflective sensor
